# Fritzing sketch CTD logger (saved by Fritzing 1.0.0rc)
breadboards: 1

parts:
  Logger = OpenLog
  CTD = IC, SIP package, 3 pins [chip_label=CTD]
  LCB = IC, SIP package, 8 pins [chip_label=LCB]
  SparkFun_Transceiver_Breakout_-_MAX1 = SparkFun Transceiver Breakout - MAX3232 [part_number=BOB-11189]  # not connected
  J1 = screw terminal, 4 pins
  SparkFun_Transceiver_Breakout_-_MAX2 = SparkFun Transceiver Breakout - MAX3232 [part_number=BOB-11189]  # not connected

nets:
  3.3V: Logger.VCC, J1.pin1
  GND: Logger.GND, CTD.pin3, J1.pin4
  N1: CTD.pin1, LCB.pin3
  N2: CTD.pin2, J1.pin2
  N3: LCB.pin4, J1.pin3

notes:
  red - 3.3V power
  blue - data from CTD (16 Hz)
  orange - data to lander control board (1 Hz)
  green - data from lander control board to CTD
  black - ground
  from CTD
  return to LCB
  R1IN (RS-232) → R1OUT (TTL)
  T1IN (TTL) → T1OUT (RS-232)

custom parts:
  SparkFun Transceiver Breakout - MAX3232: The 'must have' IC for TTL/CMOS projects finally has its own breakout board! This is the RS232 converter IC that is capable of running at 3V and communicating with 5V logic. We've taken the SOIC package MAX3232 and broken out all the pins you need to set up your RS232 to TTL connection. We've also included the necessary 0.1uF charge pump capacitors. Also remember that because the MAX3232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
